# Fritzing sketch Prototype_Remote (saved by Fritzing 0.9.3b)
breadboards: 2

parts:
  Part1 = Arduino Nano (Rev3.0) (ICSP)
  S2 = Momentary Switch [package=ksa_sealed_tac_switch]
  Part2 = NRF24L01+ Breakout Board

nets:
  GND: Part1.GND, S2.2, Part2.GND
  N1: Part1.D3, S2.3
  N2: Part1.D7, Part2.CE
  N3: Part1.D8, Part2.CS
  N4: Part1.D11/MOSI, Part2.MOSI
  N5: Part1.D12/MISO, Part2.MISO
  3V3: Part1.3V3, Part2.VCC
  N6: Part1.D13/SCK, Part2.SCK
