# Fritzing sketch Remote_Protoboard (saved by Fritzing 0.9.3b)
perfboards: 1

parts:
  S1 = Pushbutton [package="[THT]"]
  S2 = Pushbutton [package="[THT]"]
  U1 = Vibration Motor- ROB-08449 [package=vibe-motor-10mm]
  Part1 = NRF24L01+ Breakout Board
  Part2 = Arduino Nano (Rev3.0)
  Part3 = Triple Axis Accelerometer Breakout - ADXL345
  R1 = Resistor [tolerance=±5% resistance=220 package=THT]
  R2 = Resistor [tolerance=±5% resistance=220 package=THT]
  R5 = Resistor [tolerance=±5% resistance=220 package="2010 [SMD]"]
  LED2 = RGB LED (com. cathode, rgb) [package="5 mm [THT]"]
  R6 = Resistor [tolerance=±5% resistance=220 package=THT]
  BAT1 = BC9VPC [package=bc9vpc]

nets:
  N1: S1.Pin_1, S1.Pin_2, Part2.D2
  GND: S1.Pin_3, S1.Pin_4, S2.Pin_1, S2.Pin_2, U1.+, Part1.GND, Part2.GND, Part3.GND, LED2.common_cathode, BAT1.V-
  N2: S2.Pin_3, S2.Pin_4, Part2.D9
  N3: U1.-, R5.Pin_0
  VCC: Part1.VCC, Part2.3V3
  N4: Part1.CE, Part2.D7
  N5: Part1.CS, Part2.D8
  N6: Part1.SCK, Part2.D13/SCK
  N7: Part1.MOSI, Part2.D11/MOSI
  N8: Part1.MISO, Part2.D12/MISO
  N9: Part2.D3, R1.Pin_1
  N10: Part2.D4, R2.Pin_1
  N11: Part2.D5, R6.Pin_1
  N12: Part2.D6, R5.Pin_1
  N13: Part2.VIN, BAT1.V+
  5V: Part2.5V, Part3.VCC
  N14: Part2.A5, Part3.SCL
  N15: Part2.A4, Part3.SDA
  N16: R1.Pin_0, LED2.red_anode
  N17: R2.Pin_0, LED2.green_anode
  N18: LED2.blue_anode, R6.Pin_0
